// Logisim project Clocking Gate.circ as structural Verilog: 1 circuit, main circuit main
module main (
);

  D_Flip_Flop d_ff_1 ();  // open: clk, D, Q, Qn, preset, en, reset
  D_Flip_Flop d_ff_2 ();  // open: clk, D, Q, Qn, preset, en, reset
  D_Flip_Flop d_ff_3 ();  // open: clk, D, Q, Qn, preset, en, reset
  D_Flip_Flop d_ff_4 ();  // open: clk, D, Q, Qn, preset, en, reset

  // Notes on the sheet:
  //   SERIAL IN/SERIAL OUT SHIFT REGISTER
endmodule
