// Logisim project Day1.circ as structural Verilog: 1 circuit, main circuit main
module main (
  input  A0,
  input  A2,
  input  A3,
  input  A4,
  output D0
);

  wire not_1_out, not_2_out;

  not not_1 (not_1_out, A2);
  not not_2 (not_2_out, A3);
  and and_1 (D0, A0, not_1_out, not_2_out, A4);

  // Notes on the sheet:
  //   Lecture 2@Prof Mbale
  //   Always note the inital stage in a word file.
endmodule
