// Logisim project SLIDE 17.circ as structural Verilog: 1 circuit, main circuit main
module main (
  input  A,
  input  B,
  input  E,
  output D0,
  output D1,
  output D2,
  output D3
);

  wire not_1_out, not_2_out, not_3_out;

  not not_1 (not_1_out, A);
  not not_2 (not_2_out, B);
  not not_3 (not_3_out, E);
  nand nand_1 (D0, not_1_out, not_2_out, not_3_out);
  nand nand_2 (D1, not_1_out, B, not_3_out);
  nand nand_3 (D2, A, not_2_out, not_3_out);
  nand nand_4 (D3, A, B, not_3_out);
endmodule
