// Logisim project SLIDE 37.circ as structural Verilog: 1 circuit, main circuit main
module main (
  input  D0,
  input  D1,
  input  D2,
  input  D3,
  output y,
  output x,
  output V
);

  wire and_1_out, not_1_out;

  not not_1 (not_1_out, D1);
  or or_1 (x, D0, D1);
  and and_1 (and_1_out, not_1_out, D2);
  or or_2 (V, x, D2, D3);
  or or_3 (y, D0, and_1_out);
endmodule
