// Logisim project SLIDE 41 With Enable Input.circ as structural Verilog: 1 circuit, main circuit main
module main (
  input  X,
  input  X_2,
  input  Y,
  output F0,
  output F1,
  output F2,
  output F3
);

  wire not_1_out, not_2_out, not_3_out;

  not not_1 (not_1_out, X);
  not not_2 (not_2_out, X_2);
  not not_3 (not_3_out, Y);
  nand nand_1 (F0, not_2_out, not_1_out, not_3_out);
  nand nand_2 (F1, not_2_out, not_1_out, Y);
  nand nand_3 (F2, X_2, not_1_out, not_3_out);
  nand nand_4 (F3, X_2, not_1_out, Y, Y);
endmodule
