// Logisim project SLIDE 41.circ as structural Verilog: 1 circuit, main circuit main
module main (
  input  X,
  input  Y,
  output out_3,
  output out_4,
  output out_5,
  output out_6
);

  wire not_1_out, not_2_out;

  not not_1 (not_1_out, X);
  not not_2 (not_2_out, Y);
  and and_1 (out_3, not_1_out, not_2_out);
  and and_2 (out_4, not_1_out, Y);
  and and_3 (out_5, X, not_2_out);
  and and_4 (out_6, X, Y, Y);
endmodule
