// Logisim project D LATCH.circ as structural Verilog: 1 circuit, main circuit main
module main (
  input  D,
  input  D_2,
  input  D_3,
  input  D_4,
  input  E,
  input  E_2,
  input  D_5,
  input  D_6,
  input  E_3,
  input  E_4,
  output Q,
  output Q_2,
  output Q_prime,
  output Q_prime_2,
  output Q_3,
  output Q_4,
  output Q_prime_3,
  output Q_prime_4,
  output Q_5,
  output Q_6,
  output Q_prime_5,
  output Q_prime_6
);

  wire nand_1_out, nand_2_out, nand_3_out, nand_4_out, nor_1_out, nor_2_out, nor_3_out, nor_4_out, not_1_out,
       not_2_out, not_3_out, not_4_out;

  not not_1 (not_1_out, D_4);
  not not_2 (not_2_out, D_2);
  nand nand_1 (nand_1_out, D_4, E_2);
  nand nand_2 (nand_2_out, E_2, not_1_out);
  nand nand_3 (nand_3_out, D_6, E_4);
  nand nand_4 (nand_4_out, nand_3_out, E_4);
  nand nand_5 (Q_2, not_2_out, Q_prime_2);
  nand nand_6 (Q_prime_2, Q_2, D_2);
  nand nand_7 (Q_4, nand_1_out, Q_prime_4);
  nand nand_8 (Q_prime_4, Q_4, nand_2_out);
  nand nand_9 (Q_6, nand_3_out, Q_prime_6);
  nand nand_10 (Q_prime_6, Q_6, nand_4_out);
  not not_3 (not_3_out, D);
  not not_4 (not_4_out, D_3);
  nor nor_1 (nor_1_out, D_3, E);
  nor nor_2 (nor_2_out, E, not_4_out);
  nor nor_3 (nor_3_out, D_5, E_3);
  nor nor_4 (nor_4_out, nor_3_out, E_3);
  nor nor_5 (Q, not_3_out, Q_prime);
  nor nor_6 (Q_prime, Q, D);
  nor nor_7 (Q_5, nor_3_out, Q_prime_5);
  nor nor_8 (Q_prime_5, Q_5, nor_4_out);
  nor nor_9 (Q_3, nor_1_out, Q_prime_3, Q_prime_3);
  nor nor_10 (Q_prime_3, Q_3, nor_2_out);

  // Notes on the sheet:
  //   D LATCHES
  //   D LATCHES WITH ENABLE INPUTS
endmodule
