// Logisim project J K FLIPS FLOPS.circ as structural Verilog: 1 circuit, main circuit main
module main (
  input  J,
  input  K,
  output out_3,
  output out_4
);

  wire and_1_out, and_2_out, clk_out, not_1_out, or_1_out;

  Clock clk (.out(clk_out));
  not not_1 (not_1_out, K);
  and and_1 (and_1_out, out_4, J);
  and and_2 (and_2_out, not_1_out, out_3);
  or or_1 (or_1_out, and_1_out, and_2_out);
  J_K_Flip_Flop j_k_ff_1 (.J(or_1_out), .clk(clk_out), .Q(out_3), .Qn(out_4));  // open: K, preset, en, reset
endmodule
