// Logisim project SLIDE 16 - POSITIVE EDGE TRIGGERED D FLIP FLOP.circ as structural Verilog: 1 circuit, main circuit main
module main (
  input  D,
  output Q,
  output Q_prime
);

  wire CLK_out, nand_1_out, nand_2_out, nand_3_out, nand_4_out;

  Clock CLK (.out(CLK_out));
  nand nand_1 (nand_1_out, nand_4_out, nand_2_out);
  nand nand_2 (nand_2_out, nand_1_out, D);
  nand nand_3 (nand_3_out, nand_2_out, D, nand_4_out);
  nand nand_4 (nand_4_out, nand_3_out, CLK_out);
  nand nand_5 (Q, nand_2_out, Q_prime);
  nand nand_6 (Q_prime, Q, nand_3_out);

  // Notes on the sheet:
  //   POSITIVE EDGE TRIGGERED D FLIO FLOP
endmodule
