// Logisim project SLIDE 19 - D FLIP FLOP WITH ENABLE.circ as structural Verilog: 1 circuit, main circuit main
module main (
  input  D,
  input  EN,
  output Q,
  output Q_prime
);

  wire and_1_out, and_2_out, CLK_out, not_1_out, or_1_out;

  Clock CLK (.out(CLK_out));
  not not_1 (not_1_out, EN);
  and and_1 (and_1_out, D, EN);
  and and_2 (and_2_out, not_1_out, Q);
  or or_1 (or_1_out, and_1_out, and_2_out);
  D_Flip_Flop d_ff_1 (.clk(CLK_out), .D(or_1_out), .Q(Q), .Qn(Q_prime));  // open: preset, en, reset

  // Notes on the sheet:
  //   D FLIP FLOP WITH ENABLE
endmodule
