// Logisim project SLIDE11 - D FLIP FLOP CONDENSED.circ as structural Verilog: 1 circuit, main circuit main
module main (
  input  D,
  input  SET,
  input  RESET,
  output Q
);

  wire CLK_out;

  Clock CLK (.out(CLK_out));
  D_Flip_Flop #(.trigger("falling")) d_ff_1 (.clk(CLK_out), .D(D), .Q(Q), .preset(SET), .reset(RESET));  // open: Qn, en
endmodule
