// Logisim project SR LATCHES (AND OR NAND NOR).circ as structural Verilog: 1 circuit, main circuit main
module main (
  input  in_1,
  input  in_2,
  input  in_3,
  input  in_4,
  input  in_5,
  input  in_6,
  input  in_7,
  input  in_8,
  output out_9,
  output out_10,
  output out_11,
  output out_12,
  output out_13,
  output out_14,
  output out_15,
  output out_16
);

  nor nor_1 (out_9, in_1, out_11);
  nor nor_2 (out_11, out_9, in_3);
  and and_1 (out_13, in_5, out_15);
  and and_2 (out_15, out_13, in_7);
  nand nand_1 (out_10, in_2, out_12);
  nand nand_2 (out_12, out_10, in_4);
  or or_1 (out_14, in_6, out_16);
  or or_2 (out_16, out_14, in_8);

  // Notes on the sheet:
  //   SR LATCH (NOR GATES)
  //   SR LATCH (AND GATES)
  //   SR LATCH (NAND GATES)
  //   SR LATCH (OR GATES)
endmodule
