// Logisim project SLIDE 18 - SR LATCHES AND FLIP FLOPS.circ as structural Verilog: 1 circuit, main circuit main
module main (
  input  S,
  input  S_2,
  input  CLK,
  input  R,
  input  R_2,
  output Q,
  output Q_2,
  output Q_prime,
  output Q_prime_2
);

  wire nand_3_out, nand_4_out;

  nand nand_1 (Q, S_2, Q_prime);
  nand nand_2 (Q_prime, Q, R);
  nand nand_3 (nand_3_out, S, CLK);
  nand nand_4 (nand_4_out, CLK, R_2);
  nand nand_5 (Q_2, nand_3_out, Q_prime_2);
  nand nand_6 (Q_prime_2, Q_2, nand_4_out);

  // Notes on the sheet:
  //   SR LATCH
  //   SR FLIP FLOP
endmodule
