// Logisim project SLIDE 36  D LACHES WITH ENABLE.circ as structural Verilog: 1 circuit, main circuit main
module main (
  input  D,
  input  D_2,
  input  E,
  input  E_2,
  output out_5,
  output out_6,
  output out_7,
  output out_8
);

  wire nand_1_out, nand_2_out, nand_5_out, nand_6_out, not_1_out;

  nand nand_1 (nand_1_out, D, E);
  nand nand_2 (nand_2_out, nand_1_out, E);
  nand nand_3 (out_5, nand_1_out, out_7);
  nand nand_4 (out_7, out_5, nand_2_out);
  not not_1 (not_1_out, E_2);
  nand nand_5 (nand_5_out, not_1_out, D_2);
  nand nand_6 (nand_6_out, D_2, E_2);
  nand nand_7 (out_6, nand_5_out, out_8);
  nand nand_8 (out_8, out_6, nand_6_out);

  // Notes on the sheet:
  //   A.)
  //   D LATCHES WITH ENABLE INPUTS
  //   B.)
endmodule
