// Logisim project SLIDE 10.circ as structural Verilog: 1 circuit, main circuit main
module main (
  input  A0,
  input  A0_2,
  input  A1,
  input  A1_2,
  input  S,
  input  S_2,
  output Y,
  output Y_2
);

  wire and_1_out, and_2_out, not_1_out;

  not not_1 (not_1_out, S_2);
  and and_1 (and_1_out, A0, not_1_out);
  and and_2 (and_2_out, A1_2, S_2);
  or or_1 (Y_2, and_1_out, and_2_out);
  Multiplexer multiplexer_1 (.in0(A0_2), .in1(A1), .out(Y), .sel(S));  // open: en
endmodule
