// Logisim project SLIDE 29.circ as structural Verilog: 1 circuit, main circuit main
module main (
  input  G,
  input  G_2,
  input  S,
  input  S1,
  input  S0,
  output Out_0,
  output Out_0_2,
  output Out_1,
  output Out_1_2,
  output Out_2,
  output Out_3
);

  wire not_1_out, not_2_out, not_3_out;

  not not_1 (not_1_out, S);
  and and_1 (Out_0, G, not_1_out);
  and and_2 (Out_1, S, G);
  not not_2 (not_2_out, S1);
  not not_3 (not_3_out, S0);
  and and_3 (Out_0_2, G_2, not_2_out, not_3_out);
  and and_4 (Out_1_2, G_2, not_2_out, S0);
  and and_5 (Out_2, G_2, S1, not_3_out);
  and and_6 (Out_3, G_2, S1, S0);

  // Notes on the sheet:
  //   1-to-2 Demultiplexer
  //   1-to-4 Demultiplexer
endmodule
