// Logisim project SLIDE 31.circ as structural Verilog: 1 circuit, main circuit main
module main (
  input  S1,
  input  S2,
  input  in_3,
  input  S3,
  input  [2:0] in_5,
  input  I,
  output out_7,
  output O_0,
  output out_9,
  output O_1,
  output out_11,
  output out_12,
  output O_2,
  output out_14,
  output O_3,
  output out_16,
  output out_17,
  output O_4,
  output out_19,
  output O_5,
  output O_6,
  output O_7
);

  wire not_1_out, not_2_out, not_3_out, undriven;

  not not_1 (not_1_out, S1);
  not not_2 (not_2_out, S2);
  not not_3 (not_3_out, S3);
  and _0 (O_0, not_1_out, not_2_out, not_3_out, I);
  and _1 (O_1, not_1_out, not_2_out, S3, I);
  and _2 (O_2, not_1_out, S2, not_3_out, I);
  and _3 (O_3, not_1_out, not_3_out, S3, I);
  and _4 (O_4, S1, not_2_out, not_3_out, I);
  and _5 (O_5, S1, not_2_out, S3, I);
  and _6 (O_6, S2, S1, not_3_out, I);
  and _7 (O_7, S2, S1, S3, I);
  Demultiplexer #(.select(3)) demultiplexer_1 (
    .out0(out_7), .out1(out_9), .out2(out_11), .out3(out_12), .out4(out_14), .out5(out_16), .out6(out_17),
    .out7(out_19), .in(in_3), .sel(in_5), .en(undriven));

  // Notes on the sheet:
  //   1-Line-8 line Demultiplexer
  //   SYMBOLIC REPRESENTATION
endmodule
