// Logisim project SLIDE 43.circ as structural Verilog: 1 circuit, main circuit main
module main (
  input  A0,
  input  A1,
  input  A2,
  input  A3,
  input  B1,
  input  B2,
  input  B3,
  input  B4,
  input  S,
  input  E,
  output Y0,
  output Y1,
  output Y2,
  output Y3
);

  wire and_1_out, and_2_out, and_3_out, and_4_out, and_5_out, and_6_out, and_7_out, and_8_out, not_1_out,
       not_2_out, not_3_out;

  not not_1 (not_1_out, S);
  not not_2 (not_2_out, not_1_out);
  not not_3 (not_3_out, E);
  and and_1 (and_1_out, A0, not_1_out, not_3_out);
  and and_2 (and_2_out, A1, not_1_out, not_3_out);
  and and_3 (and_3_out, A2, not_1_out, not_3_out);
  and and_4 (and_4_out, A3, not_1_out, not_3_out);
  and and_5 (and_5_out, B1, not_2_out, not_3_out);
  and and_6 (and_6_out, B2, not_2_out, not_3_out);
  and and_7 (and_7_out, B3, not_2_out, not_3_out);
  and and_8 (and_8_out, B4, not_2_out, not_3_out);
  or or_1 (Y0, and_1_out, and_5_out);
  or or_2 (Y1, and_2_out, and_6_out);
  or or_3 (Y2, and_3_out, and_7_out);
  or or_4 (Y3, and_4_out, and_8_out);
endmodule
