// Logisim project SLIDE 49.circ as structural Verilog: 1 circuit, main circuit main
module main (
  input  I,
  input  in_2,
  input  S0,
  input  [1:0] in_4,
  input  S1,
  output out_6,
  output D0,
  output out_8,
  output D1,
  output out_10,
  output D2,
  output out_12,
  output D3
);

  wire not_1_out, not_2_out;

  not not_1 (not_1_out, S0);
  not not_2 (not_2_out, S1);
  and and_1 (D0, I, not_1_out, not_2_out);
  and and_2 (D1, I, S0);
  and and_3 (D2, I, not_1_out, S1);
  and and_4 (D3, I, S1, S0);
  Demultiplexer #(.select(2)) demultiplexer_1 (
    .out0(out_6), .out1(out_8), .out2(out_10), .out3(out_12), .in(in_2), .sel(in_4));  // open: en

  // Notes on the sheet:
  //   Select
  //   lines
  //   data
  //   Input
  //   {
  //   1:4 Demultiplexer
  //   Symbolic Representation
endmodule
