// Logisim project Register with Parallel Loadcirc.circ as structural Verilog: 1 circuit, main circuit main
module main (
  input  in_1,
  input  in_2,
  input  in_3,
  input  in_4,
  input  in_5,
  input  in_6,
  output out_7,
  output out_8,
  output out_9,
  output out_10
);

  wire and_1_out, and_2_out, and_3_out, and_4_out, and_5_out, and_6_out, and_7_out, and_8_out, clock_1_out,
       not_1_out, not_2_out, not_3_out, or_1_out, or_2_out, or_3_out, or_4_out;

  not not_1 (not_1_out, in_1);
  Clock clock_1 (.out(clock_1_out));
  not not_2 (not_2_out, not_1_out);
  not not_3 (not_3_out, clock_1_out);
  and and_1 (and_1_out, out_7, not_1_out);
  and and_2 (and_2_out, in_2, not_2_out);
  and and_3 (and_3_out, out_8, not_1_out);
  and and_4 (and_4_out, in_3, not_2_out);
  and and_5 (and_5_out, out_9, not_1_out);
  and and_6 (and_6_out, in_4, not_2_out);
  and and_7 (and_7_out, out_10, not_1_out);
  and and_8 (and_8_out, in_5, not_2_out);
  or or_1 (or_1_out, and_1_out, and_2_out);
  or or_2 (or_2_out, and_3_out, and_4_out);
  or or_3 (or_3_out, and_5_out, and_6_out);
  or or_4 (or_4_out, and_7_out, and_8_out);
  D_Flip_Flop d_ff_1 (.clk(not_3_out), .D(or_1_out), .Q(out_7), .en(in_6));  // open: Qn, preset, reset
  D_Flip_Flop d_ff_2 (.clk(not_3_out), .D(or_2_out), .Q(out_8), .en(in_6));  // open: Qn, preset, reset
  D_Flip_Flop d_ff_3 (.clk(not_3_out), .D(or_3_out), .Q(out_9), .en(in_6));  // open: Qn, preset, reset
  D_Flip_Flop d_ff_4 (.clk(not_3_out), .D(or_4_out), .Q(out_10), .en(in_6));  // open: Qn, preset, reset

  // Notes on the sheet:
  //   Register with Parallel Load
endmodule
