// Logisim project SLIDE 35.circ as structural Verilog: 1 circuit, main circuit main
module main (
  input  in_1,
  input  in_2,
  input  in_3,
  input  in_4,
  input  INPUT_1,
  output out_6
);

  wire and_1_out, and_2_out, and_3_out, and_4_out, and_5_out, and_6_out, CLOCK_out, d_ff_1_q, d_ff_2_q,
       d_ff_3_q, not_1_out, or_1_out, or_2_out, or_3_out;

  Clock CLOCK (.out(CLOCK_out));
  not not_1 (not_1_out, INPUT_1);
  and and_1 (and_1_out, d_ff_1_q, INPUT_1);
  D_Flip_Flop d_ff_1 (.clk(CLOCK_out), .D(in_1), .Q(d_ff_1_q));  // open: Qn, preset, en, reset
  and and_2 (and_2_out, not_1_out, in_2);
  or or_1 (or_1_out, and_1_out, and_2_out);
  D_Flip_Flop d_ff_2 (.clk(CLOCK_out), .D(or_1_out), .Q(d_ff_2_q));  // open: Qn, preset, en, reset
  and and_3 (and_3_out, d_ff_2_q, not_1_out);
  or or_2 (or_2_out, and_3_out, and_4_out);
  D_Flip_Flop d_ff_3 (.clk(CLOCK_out), .D(or_2_out), .Q(d_ff_3_q));  // open: Qn, preset, en, reset
  and and_4 (and_4_out, not_1_out, in_3);
  or or_3 (or_3_out, and_5_out, and_6_out);
  D_Flip_Flop d_ff_4 (.clk(CLOCK_out), .D(or_3_out), .Q(out_6));  // open: Qn, preset, en, reset
  and and_5 (and_5_out, d_ff_3_q, INPUT_1);
  and and_6 (and_6_out, not_1_out, in_4);

  // Notes on the sheet:
  //   PARALLEL IN/SERIAL OUT SHIFT REGISTERS
endmodule
