// Logisim project SLIDE 37.circ as structural Verilog: 1 circuit, main circuit main
module main (
  input  D0,
  input  D1,
  input  D2,
  input  D3,
  output Q0,
  output Q1,
  output Q2,
  output Q3
);

  wire CLOCK_out;

  Clock CLOCK (.out(CLOCK_out));
  D_Flip_Flop d_ff_1 (.clk(CLOCK_out), .D(D0), .Q(Q0));  // open: Qn, preset, en, reset
  D_Flip_Flop d_ff_2 (.clk(CLOCK_out), .D(D1), .Q(Q1));  // open: Qn, preset, en, reset
  D_Flip_Flop d_ff_3 (.clk(CLOCK_out), .D(D2), .Q(Q2));  // open: Qn, preset, en, reset
  D_Flip_Flop d_ff_4 (.clk(CLOCK_out), .D(D3), .Q(Q3));  // open: Qn, preset, en, reset

  // Notes on the sheet:
  //   PARALLEL IN/PARALLEL OUT SHIFT REGISTERS
endmodule
