// Logisim project SLIDE 38.circ as structural Verilog: 1 circuit, main circuit main
module main (
  input  R_L,
  input  SDI,
  output Q3,
  output Q0
);

  wire and_1_out, and_2_out, and_3_out, and_4_out, and_5_out, and_6_out, and_7_out, and_8_out, CLOCK_out,
       d_ff_2_q, d_ff_3_q, not_1_out, or_1_out, or_2_out, or_3_out, or_4_out;

  Clock CLOCK (.out(CLOCK_out));
  not not_1 (not_1_out, R_L);
  and and_1 (and_1_out, SDI, R_L);
  and and_2 (and_2_out, not_1_out, d_ff_2_q);
  or or_1 (or_1_out, and_1_out, and_2_out);
  and and_3 (and_3_out, Q0, R_L);
  D_Flip_Flop d_ff_1 (.clk(CLOCK_out), .D(or_1_out), .Q(Q0));  // open: Qn, preset, en, reset
  and and_4 (and_4_out, not_1_out, d_ff_3_q);
  or or_2 (or_2_out, and_3_out, and_4_out);
  and and_5 (and_5_out, d_ff_2_q, R_L);
  D_Flip_Flop d_ff_2 (.clk(CLOCK_out), .D(or_2_out), .Q(d_ff_2_q));  // open: Qn, preset, en, reset
  and and_6 (and_6_out, not_1_out, Q3);
  or or_3 (or_3_out, and_5_out, and_6_out);
  and and_7 (and_7_out, d_ff_3_q, R_L);
  D_Flip_Flop d_ff_3 (.clk(CLOCK_out), .D(or_3_out), .Q(d_ff_3_q));  // open: Qn, preset, en, reset
  and and_8 (and_8_out, not_1_out, SDI);
  or or_4 (or_4_out, and_7_out, and_8_out);
  D_Flip_Flop d_ff_4 (.clk(CLOCK_out), .D(or_4_out), .Q(Q3));  // open: Qn, preset, en, reset
endmodule
