// Logisim project SLIDE 39.circ as structural Verilog: 1 circuit, main circuit main
module main (
);

  wire button_1_out, clock_1_out, d_ff_1_q, d_ff_2_q, d_ff_3_q, d_ff_4_q, not_1_out, undriven, undriven_2,
       undriven_3, undriven_4, undriven_5;

  Clock clock_1 (.out(clock_1_out));
  Button button_1 (.out(button_1_out));
  not not_1 (not_1_out, clock_1_out);
  D_Flip_Flop d_ff_1 (.clk(not_1_out), .Q(d_ff_1_q), .preset(undriven_2), .en(button_1_out));  // open: D, Qn, reset
  Multiplexer #(.select(2)) multiplexer_1 (.in0(undriven));  // open: in1, in2, in3, out, sel, en
  Multiplexer multiplexer_2 ();  // open: in0, in1, out, sel, en
  D_Flip_Flop d_ff_2 (.clk(not_1_out), .Q(d_ff_2_q), .preset(undriven_3), .en(button_1_out));  // open: D, Qn, reset
  D_Flip_Flop d_ff_3 (.clk(not_1_out), .Q(d_ff_3_q), .preset(undriven_4), .en(button_1_out));  // open: D, Qn, reset
  D_Flip_Flop d_ff_4 (.clk(not_1_out), .Q(d_ff_4_q), .preset(undriven_5), .en(button_1_out));  // open: D, Qn, reset
endmodule
