// Logisim project SLIDE 52.circ as structural Verilog: 1 circuit, main circuit main
module main (
  input  SDI,
  output SDO
);

  wire CLOCK_out, d_ff_1_q, d_ff_2_q, d_ff_3_q;

  Clock CLOCK (.out(CLOCK_out));
  D_Flip_Flop d_ff_1 (.clk(CLOCK_out), .D(SDI), .Q(d_ff_1_q));  // open: Qn, preset, en, reset
  D_Flip_Flop d_ff_2 (.clk(CLOCK_out), .D(d_ff_1_q), .Q(d_ff_2_q));  // open: Qn, preset, en, reset
  D_Flip_Flop d_ff_3 (.clk(CLOCK_out), .D(d_ff_2_q), .Q(d_ff_3_q));  // open: Qn, preset, en, reset
  D_Flip_Flop d_ff_4 (.clk(CLOCK_out), .D(d_ff_3_q), .Q(SDO));  // open: Qn, preset, en, reset

  // Notes on the sheet:
  //   Q0
  //   Q1
  //   Q2
  //   Q3
endmodule
