// Logisim project Slide 15.circ as structural Verilog: 1 circuit, main circuit main
module main (
  input  A,
  input  B,
  input  E,
  output D0,
  output D1,
  output D2,
  output D4
);

  wire not_1_out, not_2_out;

  not not_1 (not_1_out, A);
  not not_2 (not_2_out, B);
  and and_1 (D0, not_1_out, not_2_out, E);
  and and_2 (D1, A, not_2_out, E);
  and and_3 (D2, B, not_1_out, E);
  and and_4 (D4, B, A, E);
endmodule
