// Logisim project Slide 17a.circ as structural Verilog: 1 circuit, main circuit main
module main (
  input  in_1,
  input  in_2,
  input  in_3,
  output out_4,
  output out_5,
  output out_6,
  output out_7
);

  wire not_1_out, not_2_out, not_3_out;

  not not_1 (not_1_out, in_2);
  not not_2 (not_2_out, in_1);
  not not_3 (not_3_out, in_3);
  nand nand_1 (out_4, not_2_out, not_1_out, not_3_out);
  nand nand_2 (out_5, not_2_out, in_2, not_3_out);
  nand nand_3 (out_6, in_1, not_1_out, not_3_out);
  nand nand_4 (out_7, in_1, in_2, not_3_out);
endmodule
