// Logisim project Slide 6 4 t0 16 Decoder.circ as structural Verilog: 1 circuit, main circuit main
module main (
  input  I3,
  input  I2,
  input  I2_2,
  input  I0,
  output O0,
  output O1,
  output O2,
  output O3,
  output O4,
  output O5,
  output O6,
  output O7,
  output O8,
  output O9,
  output O10,
  output _011,
  output _012,
  output O13,
  output _014,
  output _015
);

  wire not_1_out, not_2_out, not_3_out, not_4_out;

  not not_1 (not_1_out, I3);
  not not_2 (not_2_out, I2);
  not not_3 (not_3_out, I2);
  not not_4 (not_4_out, I0);
  and and_1 (O0, not_4_out, not_3_out, not_2_out, not_1_out);
  and and_2 (O1, I0, not_3_out, not_2_out, not_1_out);
  and and_3 (O2, not_4_out, I2, not_2_out, not_1_out);
  and and_4 (O3, I0, not_3_out, not_2_out, not_1_out);
  and and_5 (O4, not_4_out, I2, not_2_out, not_1_out);
  and and_6 (O5, I0, not_3_out, not_2_out, not_1_out);
  and and_7 (O6, not_4_out, I2, not_2_out, not_1_out);
  and and_8 (O7, I0, not_3_out, not_2_out, not_1_out);
  and and_9 (O8, not_4_out, not_3_out, not_2_out, I3);
  and and_10 (O9, not_4_out, not_3_out, not_2_out, I3);
  and and_11 (O10, not_4_out, not_3_out, not_2_out, I3);
  and and_12 (_011, I0, not_3_out, not_2_out, I3);
  and and_13 (_012, not_4_out, not_3_out, I2, I3);
  and and_14 (O13, not_4_out, not_3_out, I2, I3);
  and and_15 (_014, not_4_out, I2, I2, I3);
  and and_16 (_015, I0, I2, I2, I3);

  assign I2_2 = I2;
endmodule
